// Logisim project adder-subtractor-4bit.circ as structural Verilog: 6 circuits, main circuit ADD 1 bit
module ADD_1_bit (
  input  in_1,
  input  in_2,
  output out_3,
  output out_4
);

  and and_1 (out_4, in_1, in_2);
  xor xor_1 (out_3, in_1, in_2);
endmodule

module ADD_1_bit_complet (
  input  in_1,
  input  in_2,
  input  in_3,
  output out_4,
  output out_5
);

  wire add_1_bit_1_out_3, add_1_bit_1_out_4, add_1_bit_2_out_4;

  ADD_1_bit add_1_bit_1 (.in_1(in_2), .in_2(in_3), .out_4(add_1_bit_1_out_4), .out_3(add_1_bit_1_out_3));
  or or_1 (out_5, add_1_bit_1_out_4, add_1_bit_2_out_4);
  ADD_1_bit add_1_bit_2 (.in_1(add_1_bit_1_out_3), .in_2(in_1), .out_4(add_1_bit_2_out_4), .out_3(out_4));
endmodule

module Add_4_bit (
  input  in_1,
  input  [3:0] in_2,
  input  [3:0] in_3,
  output [3:0] out_4,
  output out_5
);

  wire add_1_bit_complet_1_out_5, add_1_bit_complet_2_out_5, add_1_bit_complet_3_out_5;

  ADD_1_bit_complet add_1_bit_complet_1 (
    .in_2(in_2[0]), .in_3(in_3[0]), .in_1(in_1), .out_5(add_1_bit_complet_1_out_5), .out_4(out_4[0]));
  ADD_1_bit_complet add_1_bit_complet_2 (
    .in_2(in_2[1]), .in_3(in_3[1]), .in_1(add_1_bit_complet_1_out_5), .out_5(add_1_bit_complet_2_out_5),
    .out_4(out_4[1]));
  ADD_1_bit_complet add_1_bit_complet_3 (
    .in_2(in_2[2]), .in_3(in_3[2]), .in_1(add_1_bit_complet_2_out_5), .out_5(add_1_bit_complet_3_out_5),
    .out_4(out_4[2]));
  ADD_1_bit_complet add_1_bit_complet_4 (
    .in_2(in_2[3]), .in_3(in_3[3]), .in_1(add_1_bit_complet_3_out_5), .out_5(out_5), .out_4(out_4[3]));
endmodule

module soustracteur_1_bit (
  input  in_1,
  input  in_2,
  input  in_3,
  output out_4,
  output out_5
);

  wire and_1_out, and_2_out, and_3_out, and_4_out, and_5_out, and_6_out, not_1_out, not_2_out, not_3_out,
       not_4_out, or_1_out;

  not not_1 (not_1_out, in_2);
  not not_2 (not_2_out, in_3);
  not not_3 (not_3_out, in_1);
  not not_4 (not_4_out, in_1);
  and and_1 (and_1_out, not_3_out, in_2, not_2_out);
  and and_2 (and_2_out, not_1_out, not_2_out, in_1);
  and and_3 (and_3_out, in_2, in_3, in_1);
  and and_4 (and_4_out, in_3, not_1_out, not_4_out);
  and and_5 (and_5_out, in_3, in_1);
  or or_1 (or_1_out, in_1, in_3);
  or or_2 (out_4, and_1_out, and_2_out, and_3_out, and_4_out);
  and and_6 (and_6_out, or_1_out, not_1_out);
  or or_3 (out_5, and_5_out, and_6_out);
endmodule

module soustracteur_4_bit (
  input  in_1,
  input  [3:0] in_2,
  input  [3:0] in_3,
  output [3:0] out_4,
  output out_5
);

  wire soustracteur_1_bit_1_out_5, soustracteur_1_bit_2_out_5, soustracteur_1_bit_3_out_5;

  soustracteur_1_bit soustracteur_1_bit_1 (
    .in_2(in_2[0]), .in_3(in_3[0]), .in_1(in_1), .out_4(out_4[0]), .out_5(soustracteur_1_bit_1_out_5));
  soustracteur_1_bit soustracteur_1_bit_2 (
    .in_2(in_2[1]), .in_3(in_3[1]), .in_1(soustracteur_1_bit_1_out_5), .out_4(out_4[1]),
    .out_5(soustracteur_1_bit_2_out_5));
  soustracteur_1_bit soustracteur_1_bit_3 (
    .in_2(in_2[2]), .in_3(in_3[2]), .in_1(soustracteur_1_bit_2_out_5), .out_4(out_4[2]),
    .out_5(soustracteur_1_bit_3_out_5));
  soustracteur_1_bit soustracteur_1_bit_4 (
    .in_2(in_2[3]), .in_3(in_3[3]), .in_1(soustracteur_1_bit_3_out_5), .out_4(out_4[3]), .out_5(out_5));
endmodule

module add_sub (
  input  in_1,
  input  [3:0] in_2,
  input  [3:0] in_3,
  output [3:0] out_4,
  output out_5
);

  wire add_4_bit_1_out_5, and_1_out, and_2_out, not_1_out, soustracteur_4_bit_1_out_5;
  wire [3:0] add_4_bit_1_out_4, soustracteur_4_bit_1_out_4;

  Add_4_bit add_4_bit_1 (.in_1(1'b0), .in_2(in_2), .in_3(in_3), .out_4(add_4_bit_1_out_4), .out_5(add_4_bit_1_out_5));
  soustracteur_4_bit soustracteur_4_bit_1 (
    .in_2(in_2), .in_3(in_3), .out_4(soustracteur_4_bit_1_out_4), .in_1(1'b0),
    .out_5(soustracteur_4_bit_1_out_5));
  and and_1 (and_1_out, soustracteur_4_bit_1_out_5, in_1);
  mux2sur4bits mux2sur4bits_1 (
    .in_2(add_4_bit_1_out_4), .in_3(soustracteur_4_bit_1_out_4), .in_1(in_1), .out_4(out_4[0]),
    .out_5(out_4[1]), .out_6(out_4[2]), .out_7(out_4[3]));
  not not_1 (not_1_out, in_1);
  and and_2 (and_2_out, add_4_bit_1_out_5, not_1_out);
  or or_1 (out_5, and_1_out, and_2_out);
endmodule
