// Logisim project register-datapath-and-ram.circ as structural Verilog: 4 circuits, main circuit Registre 4 bits
module Registre_4_bits (
  input  [3:0] Din,
  input  WE,
  input  clk,
  output [3:0] Dout
);

  Register #(.width(4)) register_1 (.D(Din), .en(WE), .Q(Dout), .clk(clk), .clr(1'b0));
endmodule

module \Chemin_de_Données  (
  input  [3:0] DIN_A,
  input  EXT_A,
  input  WE_A,
  input  [3:0] DIN_B,
  input  EXT_B,
  input  WE_B,
  input  [3:0] DIN_C,
  input  EXT_C,
  input  WE_c,
  input  [1:0] OP_X,
  input  [1:0] OP_Y,
  input  ADD_SUB,
  input  [3:0] DIN_D,
  input  EXT_D,
  input  WE_D,
  output CF,
  output OV,
  output ZF,
  output SF
);

  wire clock_1_out;
  wire [3:0] alu_1_s, mux2sur4bits_1_out_4, mux2sur4bits_2_out_4, mux2sur4bits_3_out_4, mux2sur4bits_4_out_4,
       mux32vers4_1_out_6, mux32vers4_2_out_6, RA_dout, RB_dout, RC_dout, RD_dout;

  mux2sur4bits mux2sur4bits_1 (
    .in_2(alu_1_s), .in_3(DIN_A), .in_1(EXT_A), .out_4(mux2sur4bits_1_out_4[0]),
    .out_5(mux2sur4bits_1_out_4[1]), .out_6(mux2sur4bits_1_out_4[2]), .out_7(mux2sur4bits_1_out_4[3]));
  mux2sur4bits mux2sur4bits_2 (
    .in_2(alu_1_s), .in_3(DIN_B), .in_1(EXT_B), .out_4(mux2sur4bits_2_out_4[0]),
    .out_5(mux2sur4bits_2_out_4[1]), .out_6(mux2sur4bits_2_out_4[2]), .out_7(mux2sur4bits_2_out_4[3]));
  mux2sur4bits mux2sur4bits_3 (
    .in_2(alu_1_s), .in_3(DIN_C), .in_1(EXT_C), .out_4(mux2sur4bits_3_out_4[0]),
    .out_5(mux2sur4bits_3_out_4[1]), .out_6(mux2sur4bits_3_out_4[2]), .out_7(mux2sur4bits_3_out_4[3]));
  mux2sur4bits mux2sur4bits_4 (
    .in_2(alu_1_s), .in_3(DIN_D), .in_1(EXT_D), .out_4(mux2sur4bits_4_out_4[0]),
    .out_5(mux2sur4bits_4_out_4[1]), .out_6(mux2sur4bits_4_out_4[2]), .out_7(mux2sur4bits_4_out_4[3]));
  Clock clock_1 (.out(clock_1_out));
  Registre_4_bits RA (.Din(mux2sur4bits_1_out_4), .WE(WE_A), .clk(clock_1_out), .Dout(RA_dout));
  Registre_4_bits RB (.Din(mux2sur4bits_2_out_4), .WE(WE_B), .clk(clock_1_out), .Dout(RB_dout));
  Registre_4_bits RC (.Din(mux2sur4bits_3_out_4), .WE(WE_c), .clk(clock_1_out), .Dout(RC_dout));
  Registre_4_bits RD (.Din(mux2sur4bits_4_out_4), .WE(WE_D), .clk(clock_1_out), .Dout(RD_dout));
  mux32vers4 mux32vers4_1 (.A(RA_dout), .B(RB_dout), .C(RC_dout), .D(RD_dout), .in_5(OP_X), .out_6(mux32vers4_1_out_6));
  mux32vers4 mux32vers4_2 (.A(RA_dout), .B(RB_dout), .C(RC_dout), .D(RD_dout), .in_5(OP_Y), .out_6(mux32vers4_2_out_6));
  ALU alu_1 (
    .A(mux32vers4_1_out_6), .B(mux32vers4_2_out_6), .SELECTEUR(ADD_SUB), .S(alu_1_s), .CF(CF), .OV(OV),
    .ZF(ZF), .SF(SF));
endmodule

// MUX 32 vers 4
module mux32vers4 (
  input  [3:0] A,
  input  [3:0] B,
  input  [3:0] C,
  input  [3:0] D,
  input  [1:0] in_5,
  output [3:0] out_6
);

  wire [3:0] mux2sur4bits_1_out_4, mux2sur4bits_2_out_4;

  mux2sur4bits mux2sur4bits_1 (
    .in_2(A), .in_3(B), .in_1(in_5[0]), .out_4(mux2sur4bits_1_out_4[0]), .out_5(mux2sur4bits_1_out_4[1]),
    .out_6(mux2sur4bits_1_out_4[2]), .out_7(mux2sur4bits_1_out_4[3]));
  mux2sur4bits mux2sur4bits_2 (
    .in_2(C), .in_3(D), .in_1(in_5[0]), .out_4(mux2sur4bits_2_out_4[0]), .out_5(mux2sur4bits_2_out_4[1]),
    .out_6(mux2sur4bits_2_out_4[2]), .out_7(mux2sur4bits_2_out_4[3]));
  mux2sur4bits mux2sur4bits_3 (
    .in_2(mux2sur4bits_1_out_4), .in_3(mux2sur4bits_2_out_4), .in_1(in_5[1]), .out_4(out_6[0]),
    .out_5(out_6[1]), .out_6(out_6[2]), .out_7(out_6[3]));
endmodule

module RAM (
  input  [3:0] ADRESSE,
  input  [7:0] DIN,
  input  STORE,
  input  SEL,
  input  LOAD,
  input  CLR,
  output [7:0] DOUT
);

  wire clock_1_out;

  Clock clock_1 (.out(clock_1_out));
  RAM_part #(.addrWidth(4), .bus("separate")) ram_1 (
    .addr(ADRESSE), .din(DIN), .data(DOUT), .str(STORE), .sel(SEL), .clk(clock_1_out), .ld(LOAD), .clr(CLR));
endmodule
